# Fritzing sketch EnergyMeter (saved by Fritzing 0.9.1b)
circuit board: 8.46667cm x 5.64444cm
breadboards: 1

parts:
  LED1 = smd LED [color="Red (633nm)" package="0805 [SMD]"]
  R1 = Resistor [tolerance=±5% resistance=150k package=THT]
  JP2 = Header 3 [package=molex-1x3_lock]
  U1 = 555 Timer [package="SO8 [SMD]"]
  BPW40 = LTR-301 [package=ltr-301]
  R2 = Resistor [tolerance=±5% resistance=270 package=THT]

nets:
  N1: LED1.cathode, R2.Pin_1
  N2: LED1.anode, JP2.2, U1.Pin_3
  N3: R1.Pin_0, U1.Pin_2, U1.Pin_6, BPW40.C
  3.3V: R1.Pin_1, JP2.1, U1.Pin_4, U1.Pin_8
  GND: JP2.3, U1.Pin_1, BPW40.E, R2.Pin_0
